# Fritzing sketch tlight_detect (saved by Fritzing 0.9.4)
breadboards: 1

parts:
  Part1 = Arduino Due (Rev2b)
  Part2 = Adafruit TCS34725 RGB Color Sensor [part_number="Adafruit #1334"]

nets:
  N1: Part1.IOREF, Part2.+3V3
  GND: Part1.GND, Part2.GND
  N2: Part1.D10_PWM/SS0, Part2.LED_EN
  N3: Part1.SDA1, Part2.SDA
  N4: Part1.SCL1, Part2.SCL

custom parts:
  Adafruit TCS34725 RGB Color Sensor: Your electronics can now see in dazzling color with this lovely color light sensor. We found the best color sensor on the market, the TCS34725, which has RGB and Clear light sensing elements. An IR blocking filter, integrated on-chip and localized to the color sensing photodiodes, minimizes the IR spectral component of the incoming light and allows color measurements to be made accurately. The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
